# Fritzing sketch mitsubishi-aircon-esphome (saved by Fritzing 1.0.4)

parts:
  U1 = ESP32-38PinWide [part_number=ESP32-38PinWide]
  M2 = SX1308 Module [part_number=HW-668]
  J1 = Camdenboss CTB0158-5 [part_number=CTB0158-5 package=THT]
  Part1 = I2C level shifter bidirectional
  R1 = Resistor [tolerance=±5% power=0.25W resistance=3.3k package=THT]

nets:
  N1: U1.3.3, Part1.LV
  N2: U1.GPIO14, Part1.LV2
  N3: U1.GPIO12, Part1.LV3, R1.Pin_0
  N4: U1.GND, M2.pin2
  N5: U1.GPIO13, Part1.LV1
  N6: U1.VIN, M2.pin1, Part1.HV
  N7: M2.pin3, J1.terminal_1, Part1.GND, R1.Pin_1
  N8: M2.pin4, J1.terminal_5
  N9: J1.terminal_2, Part1.HV3
  N10: J1.terminal_3, Part1.HV1
  N11: J1.terminal_4, Part1.HV2

custom parts:
  ESP32-38PinWide: Generic 38-Pin ESP32 with wide format (only access to one side of pins on a breadboard) based on Stephen Lilley's HiLetgo ESP-WROOM-32 ESP32 ESP-32S Development Board.
  SX1308 Module: SX1308 Boost Converter Module Links: Sunrom SX1308 1.2MHz 2A Step Up Converter datasheet
